// Digital circuit Lab1_ZackRoder.dig as structural Verilog
module Lab1_ZackRoder (
  input  x1,
  input  x1_2,
  output f
);

  wire and_1_out, and_2_out, not_1_out, not_2_out;

  not not_1 (not_1_out, x1_2);
  not not_2 (not_2_out, x1);
  and and_1 (and_1_out, x1, not_1_out);
  and and_2 (and_2_out, not_2_out, x1_2);
  or or_1 (f, and_1_out, and_2_out);
endmodule
