// Digital circuit adder.dig as structural Verilog
module adder (
  input  a1,
  input  a0,
  input  b1,
  input  b0,
  output s2,
  output s1,
  output s0
);

  s2 s2_1 (.a1(a1), .a0(a0), .b1(b1), .b0(b0), .s2(s2));
  s1 s1_1 (.a1(a1), .a0(a0), .b1(b1), .b0(b0), .s1(s1));
  s0 s0_1 (.a1(a1), .a0(a0), .b1(b1), .b0(b0), .s0(s0));
endmodule
