// Digital circuit lab2.dig as structural Verilog
module lab2 (
  input  a1,
  input  a0,
  input  b1,
  input  b0
);

  wire adder_1_s0, adder_1_s1, adder_1_s2;

  adder adder_1 (.a1(a1), .a0(a0), .b1(b1), .b0(b0), .s2(adder_1_s2), .s1(adder_1_s1), .s0(adder_1_s0));
  LED s2 (.in(adder_1_s2));
  LED s1 (.in(adder_1_s1));
  LED s0 (.in(adder_1_s0));
endmodule
