// Digital circuit counter.dig as structural Verilog
module counter (
  input  en,
  input  clk,
  output b0,
  output b1,
  output b2,
  output b3,
  output c
);

  wire and_1_out, and_2_out, and_3_out;

  and and_1 (and_1_out, b0, en);
  and and_2 (and_2_out, b1, and_1_out);
  and and_3 (and_3_out, b2, and_2_out);
  JK_FF jk_ff_1 (.J(en), .C(clk), .K(en), .Q(b0));  // open: nQ
  JK_FF jk_ff_2 (.J(and_1_out), .C(clk), .K(and_1_out), .Q(b1));  // open: nQ
  JK_FF jk_ff_3 (.J(and_2_out), .C(clk), .K(and_2_out), .Q(b2));  // open: nQ
  JK_FF jk_ff_4 (.J(and_3_out), .C(clk), .K(and_3_out), .Q(b3));  // open: nQ
  and and_4 (c, b3, and_3_out);
endmodule
