// Digital circuit lab3.dig as structural Verilog
module lab3 (
  input  enable,
  input  clk
);

  wire counter_1_b0, counter_1_b1, counter_1_b2, counter_1_b3, ssdd_1_seg0, ssdd_1_seg1, ssdd_1_seg2,
       ssdd_1_seg3, ssdd_1_seg4, ssdd_1_seg5, ssdd_1_seg6;

  counter counter_1 (
    .en(enable), .clk(clk), .b0(counter_1_b0), .b1(counter_1_b1), .b2(counter_1_b2), .b3(counter_1_b3));  // open: c
  ssdd ssdd_1 (
    .A(counter_1_b3), .B(counter_1_b2), .C(counter_1_b1), .D(counter_1_b0), .seg0(ssdd_1_seg0),
    .seg1(ssdd_1_seg1), .seg2(ssdd_1_seg2), .seg3(ssdd_1_seg3), .seg4(ssdd_1_seg4), .seg5(ssdd_1_seg5),
    .seg6(ssdd_1_seg6));
  Seven_Seg seven_seg_1 (
    .a(ssdd_1_seg0), .b(ssdd_1_seg1), .c(ssdd_1_seg2), .d(ssdd_1_seg3), .e(ssdd_1_seg4), .f(ssdd_1_seg5),
    .g(ssdd_1_seg6), .dp(1'b0));
endmodule
