// Digital circuit lab3_test.dig as structural Verilog
module lab3_test (
  input  A,
  input  B,
  input  C,
  input  D
);

  wire ssdd_1_seg0, ssdd_1_seg1, ssdd_1_seg2, ssdd_1_seg3, ssdd_1_seg4, ssdd_1_seg5, ssdd_1_seg6;

  ssdd ssdd_1 (
    .A(A), .B(B), .C(C), .D(D), .seg0(ssdd_1_seg0), .seg1(ssdd_1_seg1), .seg2(ssdd_1_seg2),
    .seg3(ssdd_1_seg3), .seg4(ssdd_1_seg4), .seg5(ssdd_1_seg5), .seg6(ssdd_1_seg6));
  Seven_Seg seven_seg_1 (
    .a(ssdd_1_seg0), .b(ssdd_1_seg1), .c(ssdd_1_seg2), .d(ssdd_1_seg3), .e(ssdd_1_seg4), .f(ssdd_1_seg5),
    .g(ssdd_1_seg6), .dp(1'b0));
endmodule
