// Digital circuit seg0.dig as structural Verilog
module seg0 (
  input  A,
  input  B,
  input  C,
  input  D,
  output seg0
);

  wire and_1_out, and_2_out, and_3_out, and_4_out, and_5_out, and_6_out;

  and and_1 (and_1_out, B, C);
  and and_2 (and_2_out, ~B, ~D);  // And
  and and_3 (and_3_out, ~A, B, D);  // And
  and and_4 (and_4_out, A, ~C, ~D);  // And
  and and_5 (and_5_out, A, ~B, ~C);  // And
  and and_6 (and_6_out, ~A, C);  // And
  or or_1 (seg0, and_1_out, and_2_out, and_3_out, and_4_out, and_5_out, and_6_out);
endmodule
