// Digital circuit seg1.dig as structural Verilog
module seg1 (
  input  A,
  input  B,
  input  C,
  input  D,
  output seg1
);

  wire and_1_out, and_2_out, and_3_out, and_4_out, and_5_out;

  and and_1 (and_1_out, ~A, ~B);  // And
  and and_2 (and_2_out, ~B, ~D);  // And
  and and_3 (and_3_out, A, ~C, D);  // And
  and and_4 (and_4_out, ~A, ~C, ~D);  // And
  and and_5 (and_5_out, ~A, C, D);  // And
  or or_1 (seg1, and_1_out, and_2_out, and_3_out, and_4_out, and_5_out);
endmodule
