// Digital circuit seg3.dig as structural Verilog
module seg3 (
  input  A,
  input  B,
  input  C,
  input  D,
  output seg3
);

  wire and_1_out, and_2_out, and_3_out, and_4_out, and_5_out, and_6_out;

  and and_1 (and_1_out, A, ~C);  // And
  and and_2 (and_2_out, ~B, ~C, ~D);  // And
  and and_3 (and_3_out, ~B, C, D);  // And
  and and_4 (and_4_out, ~A, C, ~D);  // And
  and and_5 (and_5_out, B, C, ~D);  // And
  and and_6 (and_6_out, B, ~C, D);  // And
  or or_1 (seg3, and_1_out, and_2_out, and_3_out, and_4_out, and_5_out, and_6_out);
endmodule
