// Digital circuit seg4.dig as structural Verilog
module seg4 (
  input  A,
  input  B,
  input  C,
  input  D,
  output seg4
);

  wire and_1_out, and_2_out, and_3_out, and_4_out;

  and and_1 (and_1_out, C, ~D);  // And
  and and_2 (and_2_out, A, B);
  and and_3 (and_3_out, A, C);
  and and_4 (and_4_out, ~B, ~C, ~D);  // And
  or or_1 (seg4, and_1_out, and_2_out, and_3_out, and_4_out);
endmodule
