// Digital circuit seg6.dig as structural Verilog
module seg6 (
  input  A,
  input  B,
  input  C,
  input  D,
  output seg6
);

  wire and_1_out, and_2_out, and_3_out, and_4_out, and_5_out;

  and and_1 (and_1_out, A, ~B);  // And
  and and_2 (and_2_out, C, ~D);  // And
  and and_3 (and_3_out, A, D);
  and and_4 (and_4_out, ~A, B, ~C);  // And
  and and_5 (and_5_out, ~A, ~B, C);  // And
  or or_1 (seg6, and_1_out, and_2_out, and_3_out, and_4_out, and_5_out);
endmodule
