// Digital circuit ssdd.dig as structural Verilog
module ssdd (
  input  A,
  input  B,
  input  C,
  input  D,
  output seg0,
  output seg1,
  output seg2,
  output seg3,
  output seg4,
  output seg5,
  output seg6
);

  seg0 seg0_1 (.A(A), .B(B), .C(C), .D(D), .seg0(seg0));
  seg1 seg1_1 (.A(A), .B(B), .C(C), .D(D), .seg1(seg1));
  seg2 seg2_1 (.A(A), .B(B), .C(C), .D(D), .seg2(seg2));
  seg3 seg3_1 (.A(A), .B(B), .C(C), .D(D), .seg3(seg3));
  seg4 seg4_1 (.A(A), .B(B), .C(C), .D(D), .seg4(seg4));
  seg5 seg5_1 (.A(A), .B(B), .C(C), .D(D), .seg5(seg5));
  seg6 seg6_1 (.A(A), .B(B), .C(C), .D(D), .seg6(seg6));
endmodule
