// Digital circuit s0.dig as structural Verilog
module s0 (
  input  a1,
  input  a0,
  input  b1,
  input  b0,
  output s0
);

  wire and_1_out, and_2_out;

  and and_1 (and_1_out, a0, ~b0);  // And
  and and_2 (and_2_out, ~a0, b0);  // And
  or or_1 (s0, and_1_out, and_2_out);
endmodule
