// Digital circuit s1.dig as structural Verilog
module s1 (
  input  a1,
  input  a0,
  input  b1,
  input  b0,
  output s1
);

  wire and_1_out, and_2_out, and_3_out, and_4_out, and_5_out, and_6_out, or_1_out, or_2_out, or_3_out;

  and and_1 (and_1_out, a1, ~b1, ~b0);  // And
  and and_2 (and_2_out, a1, ~a0, ~b1);  // And
  and and_3 (and_3_out, ~a1, a0, ~b1, b0);  // And
  and and_4 (and_4_out, a1, a0, b1, b0);
  and and_5 (and_5_out, ~a1, ~a0, b1);  // And
  and and_6 (and_6_out, ~a1, b1, ~b0);  // And
  or or_1 (or_1_out, and_1_out, and_2_out);
  or or_2 (or_2_out, and_3_out, and_4_out);
  or or_3 (or_3_out, and_5_out, and_6_out);
  or or_4 (s1, or_1_out, or_2_out, or_3_out);
endmodule
