// Digital circuit s2.dig as structural Verilog
module s2 (
  input  a1,
  input  a0,
  input  b1,
  input  b0,
  output s2
);

  wire and_1_out, and_2_out, and_3_out;

  and and_1 (and_1_out, a1, b1);
  and and_2 (and_2_out, a1, a0, b0);
  and and_3 (and_3_out, a0, b1, b0);
  or or_1 (s2, and_1_out, and_2_out, and_3_out);
endmodule
